# Fritzing sketch Project (saved by Fritzing 0.9.3b)

parts:
  Part1 = Arduino Mega 2560 (Rev3)
  S2 = SWITCH-MOMENTARY-2 [package=tactile_switch_smd-2]
  S3 = SWITCH-MOMENTARY-2 [package=tactile_switch_smd-2]
  S4 = SWITCH-MOMENTARY-2 [package=tactile_switch_smd-2]
  S6 = SWITCH-MOMENTARY-2 [package=tactile_switch_smd-2]
  Disp1 = LBT2088AH [part_number=LBT2088AH]
  U1 = MAX7219 [package=dil24]
  R1 = Resistor [tolerance=±5% resistance=220 package="0805 [SMD]"]
  U2 = POT_SWITCH [package=pot_pth]

nets:
  N1: Part1.A15, U2.G$2_1
  GND: Part1.GND, S2.1, S3.1, S4.1, S6.1, U1.GND, U1.GND2, U2.G$1_E
  N2: Part1.D10_PWM, U1.LOAD
  N3: Part1.D9_PWM, U1.CLK
  N4: Part1.D8_PWM, U1.DIN
  5V: Part1.5V, U1.VCC, R1.Pin_1, U2.G$1_A
  N5: Part1.D4_PWM, S3.2
  N6: Part1.D5_PWM, S4.2
  N7: Part1.D6_PWM, S6.2
  N8: Part1.D7_PWM, S2.2
  N9: Disp1.pin1, U1.DIG3
  N10: Disp1.pin2, U1.DIG1
  N11: Disp1.pin_3, U1.SEGA
  N12: Disp1.pin_4, U1.SEGB
  N13: Disp1.pin_5, U1.DIG0
  N14: Disp1.pin_6, U1.SEGD
  N15: Disp1.pin_7, U1.DIG2
  N16: Disp1.pin_8, U1.DIG5
  N17: Disp1.pin_9, U1.DIG7
  N18: Disp1.pin_10, U1.SEGC
  N19: Disp1.pin_11, U1.SEGE
  N20: Disp1.pin_12, U1.DIG4
  N21: Disp1.pin_13, U1.SEGDP
  N22: Disp1.pin_14, U1.DIG6
  N23: Disp1.pin_15, U1.SEGF
  N24: Disp1.pin_16, U1.SEGG
  N25: U1.ISET, R1.Pin_0
